# Fritzing sketch Matrix LED (saved by Fritzing 0.9.6b)
breadboards: 1

parts:
  U1 = WS2812 RGB LED strip
  Mod1 = Raspberry Pi 4B
  Part1 = Logic Level Converter
  M1 = RioRand LM2596

nets:
  GND: U1.GND, Mod1.GND, Part1.GND, M1.Pin_4
  N1: U1.VCC, Part1.HV, M1.Pin_3
  N2: U1.DIN, Part1.TX_HV
  N3: Mod1.3V3, Part1.LV
  N4: Mod1.GPIO6, Part1.TX_LV

notes:
  3.3V
  Ground
  5.0V
  Hot
  DATA
  DATA GPIO 12/32
  Raspberry PI 3.3V Logic Level
  WS2812 5V Logic Level

custom parts:
  WS2812 RGB LED strip: WS2812 strip
